// Digital circuit HW1-4-bit-full-adder.dig as structural Verilog
module HW1_4_bit_full_adder (
  input  [3:0] in_1,
  input  [3:0] in_3,
  output [3:0] out_2
);

  wire full_adder_1_p3, full_adder_2_p3, full_adder_3_p3;

  // full_adder full_adder_1: pin names not known; wires that end beside it: in_1[3], in_3[3], full_adder_1_p3, out_2[3]
  // full_adder full_adder_2: pin names not known; wires that end beside it: in_1[2], in_3[2], full_adder_2_p3, out_2[2], full_adder_1_p3
  // full_adder full_adder_3: pin names not known; wires that end beside it: in_1[1], in_3[1], full_adder_3_p3, out_2[1], full_adder_2_p3
  // full_adder full_adder_4: pin names not known; wires that end beside it: in_1[0], in_3[0], 1'b0, out_2[0], full_adder_3_p3
endmodule
