// Digital circuit HW1_full_adder.dig as structural Verilog
module HW1_full_adder (
  input  A,
  input  B,
  input  Cin,
  output Sum,
  output C_out
);

  wire and_1_out, and_2_out, and_3_out, and_4_out, and_5_out, and_6_out, and_7_out;

  and and_1 (and_1_out, A, B);
  and and_2 (and_2_out, A, Cin);
  and and_3 (and_3_out, B, Cin);
  or or_1 (C_out, and_1_out, and_2_out, and_3_out);
  and and_4 (and_4_out, ~A, ~B, Cin);  // And
  and and_5 (and_5_out, ~A, B, ~Cin);  // And
  and and_6 (and_6_out, A, ~B, ~Cin);  // And
  and and_7 (and_7_out, A, B, Cin);
  or or_2 (Sum, and_4_out, and_5_out, and_6_out, and_7_out);
endmodule
