// Digital circuit hw1_multiplier.dig as structural Verilog
module hw1_multiplier (
  input  [1:0] A,
  input  [1:0] B,
  output p0,
  output p1,
  output p2,
  output p3
);

  wire and_2_out, and_3_out, and_4_out, and_5_out;

  and and_1 (p0, A[0], B[0]);
  and and_2 (and_2_out, B[1], A[0]);
  and and_3 (and_3_out, A[1], B[0]);
  and and_4 (and_4_out, A[1], B[1]);
  xor xor_1 (p1, and_2_out, and_3_out);
  and and_5 (and_5_out, and_2_out, and_3_out);
  xor xor_2 (p2, and_5_out, and_4_out);
  and and_6 (p3, and_5_out, and_4_out);
endmodule
